# Fritzing sketch BierP30_ArduinoMega_mitTemp (saved by Fritzing 0.9.3b)
perfboards: 9
stripboards: 1

parts:
  Bauteil1 = Arduino Mega 2560 (Rev3)
  8x8_LED_Modul_mit_MAX2 = 8x8 LED Modul mit MAX7219 [package=THT]
  Mod2 = KY-019 5V Relay Module [package="Breakout board"]
  NEOPIXEL2 = Neopixel Strip -- Black (30/m) [part_number=1376]
  Bauteil3 = RFID-RC522-v2
  U2 = LM2596 step down module
  DS1 = DS18B20 1-Wire Temperature Sensor Probe Cable  # not connected

nets:
  3V3: Bauteil1.3V3, Bauteil3.3.3V
  N1: Bauteil1.D3_PWM, 8x8_LED_Modul_mit_MAX2.CS_Eingang
  N2: Bauteil1.D4_PWM, NEOPIXEL2.Din
  N3: Bauteil1.D5_PWM, Mod2.S
  N4: Bauteil1.D6_PWM, Bauteil3.RST
  N5: Bauteil1.D7_PWM, Bauteil3.SDA
  N6: Bauteil1.D50, Bauteil3.MISO
  N7: U2.IN-, U2.OUT-

notes:
  Data=gelb, nicht weiß!

custom parts:
  KY-019 5V Relay Module: KY-019 5V Relay module, used to control AC circuits. (Special thanks to vanepp for fixing the PCB holes and other errors)
  Neopixel Strip -- Black (30/m): These NeoPixel strips have 30 digitally-addressable pixel LEDs per meter and are very affordable and are only 12.5 mm wide, 10 mm if you remove the strip from the casing.
  RFID-RC522-v2: A simple China made RFID-RC522 Reader; do check the pin labels, as this is a MFRC522 based clone.
  LM2596 step down module: LM2596 DC-DC step down power supply module 3 A.
